# Fritzing sketch PCB (saved by Fritzing 0.9.3b)
breadboards: 1

parts:
  IC1 = ADS1115 16-bit ADC Breakout
  Part1 = Soil Moisture Sensor
  Raspberry_Pi1 = Raspberry Pi B rev2
  R1 = Photocell (LDR) [package=THT]
  C1 = Electrolytic Capacitor [capacitance=1µF voltage=6.3V package="100 mil [THT, electrolytic]"]

nets:
  VDD: IC1.VDD, Part1.VCC, Raspberry_Pi1.3V3, R1.pin_0
  GND: IC1.GND, Part1.GND, Raspberry_Pi1.GND, C1.-
  N1: IC1.SCL, Raspberry_Pi1.GPIO_3
  N2: IC1.SDA, Raspberry_Pi1.GPIO_2
  N3: IC1.A0, Part1.SIG
  N4: R1.pin_1, C1.+

custom parts:
  ADS1115 16-bit ADC Breakout: ADS1015 12-bit I2C ADC+PGA Breakout
