# Fritzing sketch RaspiGuard Schematic (saved by Fritzing 0.9.3b)
breadboards: 1

parts:
  Part1 = Soil Moisture Sensor
  IC1 = ADS1115 16-bit ADC Breakout
  Raspberry_Pi2 = Raspberry Pi B rev2
  S5 = Magnetic Door Switch [package=reed_switch_plastic]
  J1 = Piezo Speaker
  R3 = Resistor [tolerance=±5% resistance=10 package=THT]
  R4 = PHOTOCELL [package=photocell]

nets:
  GND: Part1.GND, IC1.GND, Raspberry_Pi2.GND, S5.2, R3.Pin_0
  N1: Part1.SIG, IC1.A1
  VCC: Part1.VCC, IC1.VDD, Raspberry_Pi2.3V3, J1.pin2, R4.P$2
  N2: IC1.SCL, Raspberry_Pi2.GPIO_3
  N3: IC1.SDA, Raspberry_Pi2.GPIO_2
  N4: IC1.A0, R3.Pin_1, R4.P$1
  N5: Raspberry_Pi2.GPIO_18, J1.pin1
  N6: Raspberry_Pi2.GPIO_4, S5.1

custom parts:
  ADS1115 16-bit ADC Breakout: ADS1015 12-bit I2C ADC+PGA Breakout
